# Fritzing sketch Steckplan (saved by Fritzing 1.0.4)
breadboards: 2

parts:
  Bauteil93 = 12 NeoPixel Ring [part_number=1643]
  Bauteil94 = Triple Axis Accelerometer Breakout - ADXL335
  Bauteil95 = PN532 Elechouse RFID NFC Module V3
  R23 = Resistor [tolerance=±5% resistance=390 power=0.25W package=THT]
  C22 = Electrolytic Capacitor [capacitance=100nF voltage=35V package="100 mil [THT, electrolytic]"]
  C23 = Electrolytic Capacitor [capacitance=100nF voltage=35V package="100 mil [THT, electrolytic]"]
  A23 = ESP32-C6 devkit
  R24 = Resistor [tolerance=±5% resistance=2.2k power=0.25W package=THT]
  R25 = Resistor [tolerance=±5% resistance=2.2k power=0.25W package=THT]
  Bauteil96 = 12 NeoPixel Ring [part_number=1643]
  Bauteil98 = PN532 Elechouse RFID NFC Module V3
  R27 = Resistor [tolerance=±5% resistance=2.2k power=0.25W package=THT]
  R28 = Resistor [tolerance=±5% resistance=390 power=0.25W package=THT]
  C24 = Electrolytic Capacitor [capacitance=100nF voltage=35V package="100 mil [THT, electrolytic]"]
  C25 = Electrolytic Capacitor [capacitance=100nF voltage=35V package="100 mil [THT, electrolytic]"]
  A24 = ESP32-C6 devkit
  R26 = Resistor [tolerance=±5% power=0.25W resistance=2.2k package=THT]

nets:
  N1: Bauteil93.IN, R23.Pin_1
  GND: Bauteil93.GND, Bauteil94.GND, Bauteil95.GND, C22.-, C23.-, A23.Pin_1, A23.Pin_17, A23.Pin_30
  N2: Bauteil93.VDD, C22.+, A23.Pin_15, A23.Pin_16
  VIN: Bauteil94.VIN, Bauteil95.VCC, C23.+, R24.Pin_0
  N3: Bauteil94.SDA, A23.Pin_6, R25.Pin_1
  N4: Bauteil94.SCL, A23.Pin_7, R24.Pin_1
  N5: R23.Pin_0, A23.Pin_5
  N6: Bauteil96.IN, R28.Pin_1
  GND_2: Bauteil96.GND, Bauteil98.GND, C24.-, C25.-, A24.Pin_1, A24.Pin_17, A24.Pin_30
  N7: Bauteil96.VDD, C24.+, A24.Pin_15, A24.Pin_16
  N8: Bauteil98.VCC, C25.+, R26.Pin_0
  N9: R27.Pin_1, A24.Pin_6
  N10: R28.Pin_0, A24.Pin_5
  N11: A24.Pin_7, R26.Pin_1

custom parts:
  12 NeoPixel Ring: 12 ultra bright smart LED NeoPixels are arranged in a circle with 1.5" (37mm) outer diameter. The rings are 'chainable' - connect the output pin of one to the input pin of another. Use only one microcontroller pin to control as many as you can chain together! Each LED is addressable as the driver chip is inside the LED. Each one has ~18mA constant current drive so the color will be very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
  Triple Axis Accelerometer Breakout - ADXL335: Accelerometer for sensing three-dimensional orientation/acceleration on a breakout board. Compatible to the ADXL3xx series of sensor chips.
  PN532 Elechouse RFID NFC Module V3: NFC is a popular technology in recent years. We often heard this work while smart phone company such as Samsung or HTC introduces their latest high-end phones. Almost all the high-end phone in the market support NFC. Near field communication (NFC) is a set of standards for smart phones and similar devices to establish radio communication with each other by touching them together or bringing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
  ESP32-C6 devkit: ESP32 / ESP32-C6 WiFi+Bluetooth Internet Of Things Dual Type-C Development Board Core Board ESP32-C6-DevKit.
