# Fritzing sketch Steckplan (saved by Fritzing 1.0.4)
breadboards: 1

parts:
  Bauteil90 = 12 NeoPixel Ring [part_number=1643]
  Bauteil91 = Triple Axis Accelerometer Breakout - ADXL335
  Bauteil92 = PN532 Elechouse RFID NFC Module V3
  R22 = Resistor [tolerance=±5% resistance=390 power=0.25W package=THT]
  C20 = Electrolytic Capacitor [capacitance=100nF voltage=35V package="100 mil [THT, electrolytic]"]
  C21 = Electrolytic Capacitor [capacitance=100nF voltage=35V package="100 mil [THT, electrolytic]"]
  A22 = ESP32-C6 devkit

nets:
  N1: Bauteil90.IN, R22.Pin_1
  GND: Bauteil90.GND, Bauteil91.GND, Bauteil92.GND, C20.-, C21.-, A22.Pin_1, A22.Pin_17, A22.Pin_30
  N2: Bauteil90.VDD, C20.+, A22.Pin_15, A22.Pin_16
  VIN: Bauteil91.VIN, Bauteil92.VCC, C21.+
  N3: Bauteil91.SDA, A22.Pin_6
  N4: Bauteil91.SCL, A22.Pin_7
  N5: R22.Pin_0, A22.Pin_5

custom parts:
  12 NeoPixel Ring: 12 ultra bright smart LED NeoPixels are arranged in a circle with 1.5" (37mm) outer diameter. The rings are 'chainable' - connect the output pin of one to the input pin of another. Use only one microcontroller pin to control as many as you can chain together! Each LED is addressable as the driver chip is inside the LED. Each one has ~18mA constant current drive so the color will be very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
  Triple Axis Accelerometer Breakout - ADXL335: Accelerometer for sensing three-dimensional orientation/acceleration on a breakout board. Compatible to the ADXL3xx series of sensor chips.
  PN532 Elechouse RFID NFC Module V3: NFC is a popular technology in recent years. We often heard this work while smart phone company such as Samsung or HTC introduces their latest high-end phones. Almost all the high-end phone in the market support NFC. Near field communication (NFC) is a set of standards for smart phones and similar devices to establish radio communication with each other by touching them together or bringing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
  ESP32-C6 devkit: ESP32 / ESP32-C6 WiFi+Bluetooth Internet Of Things Dual Type-C Development Board Core Board ESP32-C6-DevKit.
